// Logisim project 1 2bit ram cell.circ as structural Verilog: 1 circuit, main circuit main
module main (
  input  R_W_prime,
  input  DATA,
  input  SELECT,
  input  DATA_2,
  output out_5,
  output out_6
);

  wire and_1_out, and_2_out, and_4_out, and_5_out, clock_1_out, not_1_out, not_2_out, not_3_out, not_4_out,
       s_r_ff_1_q, s_r_ff_2_q;

  not not_1 (not_1_out, R_W_prime);
  not not_2 (not_2_out, DATA);
  and and_1 (and_1_out, DATA, not_1_out);
  and and_2 (and_2_out, not_2_out, not_1_out);
  Clock clock_1 (.out(clock_1_out));
  S_R_Flip_Flop s_r_ff_1 (
    .S(and_1_out), .clk(clock_1_out), .R(and_2_out), .Q(s_r_ff_1_q), .en(SELECT));  // open: Qn, preset, reset
  and and_3 (out_5, s_r_ff_1_q, R_W_prime);
  not not_3 (not_3_out, R_W_prime);
  not not_4 (not_4_out, DATA_2);
  and and_4 (and_4_out, DATA_2, not_3_out);
  and and_5 (and_5_out, not_4_out, not_3_out);
  S_R_Flip_Flop s_r_ff_2 (
    .S(and_4_out), .clk(clock_1_out), .R(and_5_out), .Q(s_r_ff_2_q), .en(SELECT));  // open: Qn, preset, reset
  and and_6 (out_6, s_r_ff_2_q, R_W_prime);

  // Notes on the sheet:
  //   0 -WRITE
  //   1-READ
  //   0 -WRITE
  //   1-READ
endmodule
